# Fritzing sketch ESP12Eboard (saved by Fritzing 0.9.3b)
circuit board: 3.30235cm x 5.90144cm
breadboards: 1

parts:
  ANT = WeMos D1 Mini
  I2C1 = I2C male header [form="♂ (male)" package=THT]
  I2C2 = I2C male header [form="♂ (male)" package=THT]
  I2C3 = I2C male header [form="♂ (male)" package=THT]
  RTC = I2C male header [form="♂ (male)" package=THT]
  LCD = I2C male header [form="♂ (male)" package=THT]
  GPIO = male pin header, 3 pins [form="♂ (male)"]
  D7 = Header 3 [package=molex-1x3_lock]
  D5 = Header 3 [package=molex-1x3_lock]
  D6 = Header 3 [package=molex-1x3_lock]

nets:
  3.3V: ANT.3V3, I2C1.Vcc, I2C2.Vcc, I2C3.Vcc, RTC.Vcc, LCD.Vcc, D7.2, D5.2, D6.2
  SCL: ANT.D1, I2C1.SCL, I2C2.SCL, I2C3.SCL, RTC.SCL, LCD.SCL
  SDA: ANT.D2, I2C1.SDA_line, I2C2.SDA_line, I2C3.SDA_line, RTC.SDA_line, LCD.SDA_line
  D5/IO 14: ANT.D5, GPIO.pin3, D5.3
  D6/IO 12: ANT.D6, GPIO.pin2, D6.3
  D7/IO 13: ANT.D7, GPIO.pin1, D7.3
  0V: ANT.G, I2C1.GND, I2C2.GND, I2C3.GND, RTC.GND, LCD.GND, D7.1, D5.1, D6.1

custom parts:
  WeMos D1 Mini: The D1 mini is a mini wifi board based on ESP-8266EX.
  I2C male header: Male header connection for I2C devices
